# Fritzing sketch led-protoboard (saved by Fritzing 0.9.3b)
breadboards: 1

parts:
  Componente1 = Arduino Uno (Rev3)
  LED1 = LED - 5mm [color="Red (633nm)" package="5 mm [THT]"]
  R1 = Resistor [tolerance=±5% resistance=220 package=THT]
  R2 = Resistor [tolerance=±5% resistance=220 package=THT]
  LED2 = smd LED [color="Yellow (595nm)" package="0603 [SMD]"]
  LED3 = smd LED [color="Green (570nm)" package="0603 [SMD]"]
  R3 = Resistor [tolerance=±5% resistance=220 package=THT]

nets:
  N1: Componente1.D2, LED1.cathode
  N2: Componente1.D3_PWM, LED2.cathode
  N3: Componente1.D4, LED3.cathode
  N4: Componente1.GND, R1.Pin_1, R2.Pin_1, R3.Pin_1
  N5: LED1.anode, R1.Pin_0
  N6: R2.Pin_0, LED2.anode
  N7: LED3.anode, R3.Pin_0
